# Fritzing sketch swnt-reactor (saved by Fritzing 0.9.0b)
breadboards: 1

parts:
  R1_1 = Resistor [tolerance=±5% resistance=10k package=THT]
  R1_2 = Resistor [tolerance=±5% resistance=1k package=THT]
  R1_3 = Resistor [tolerance=±5% resistance=10k package=THT]
  D1 = Rectifier Diode [part_number=1N4001 package="300 mil [THT]"]
  Arduino_Uno = Arduino Uno (Rev3)
  R2_1 = Resistor [tolerance=±5% resistance=10k package=THT]
  R2_3 = Resistor [tolerance=±5% resistance=10k package=THT]
  D2 = Rectifier Diode [part_number=1N4001 package="300 mil [THT]"]
  R3_1 = Resistor [tolerance=±5% resistance=10k package=THT]
  R3_2 = Resistor [tolerance=±5% resistance=1k package=THT]
  R3_3 = Resistor [tolerance=±5% resistance=10k package=THT]
  R4 = Resistor [tolerance=±5% resistance=22k package=THT]
  C4 = Electrolytic Capacitor [capacitance=10µF package="100 mil [THT, electrolytic]"]
  R5_1 = Resistor [tolerance=±5% resistance=3.3k package=THT]
  C6 = Electrolytic Capacitor [capacitance=10µF package="100 mil [THT, electrolytic]"]
  R5_2 = Resistor [tolerance=±5% resistance=1k package=THT]
  R6 = Resistor [tolerance=±5% resistance=22k package=THT]
  MAX232 = RS232 Transceiver [package=dil16]
  C232_3 = Electrolytic Capacitor [capacitance=10µF package="100 mil [THT, electrolytic]"]
  C232_1 = Electrolytic Capacitor [capacitance=10µF package="100 mil [THT, electrolytic]"]
  C232_2 = Electrolytic Capacitor [capacitance=10µF package="100 mil [THT, electrolytic]"]
  C232_4 = Electrolytic Capacitor [capacitance=10µF package="100 mil [THT, electrolytic]"]
  D3 = Rectifier Diode [part_number=1N4001 breakdown_voltage=3.6V package="300 mil [THT]"]
  D-SUB = DB9 Connector [package=db9]
  R2_2 = Resistor [tolerance=±5% resistance=10k package=THT]
  Q1 = NPN-Transistor [package="TO92 [THT]"]
  R7 = Resistor [tolerance=±5% resistance=1k package=THT]
  R8 = Resistor [tolerance=±5% resistance=1k package=THT]
  V1 = DC Power [voltage=30V]

nets (from the schematic view):
  N1: R1_1.Pin_0, R1_3.Pin_0
  N2: R1_1.Pin_1, R1_2.Pin_0, Arduino_Uno.A1
  GND: R1_2.Pin_1, D1.cathode, Arduino_Uno.GND, D2.cathode, R3_2.Pin_1, C4.+, C6.+, R5_2.Pin_1, MAX232.GND, C232_4.+, D3.cathode, D-SUB.5, R2_2.Pin_1, Q1.E, V1.V-
  N3: R1_3.Pin_1, D1.anode, Arduino_Uno.A0
  N4: Arduino_Uno.A2, R2_3.Pin_1, D2.anode
  N5: Arduino_Uno.A3, R2_1.Pin_1, R2_2.Pin_0
  N6: Arduino_Uno.A4/SDA, R3_3.Pin_1, D3.anode
  N7: Arduino_Uno.A5/SCL, R3_1.Pin_1, R3_2.Pin_0
  N8: Arduino_Uno.D8, MAX232.T2IN
  N9: Arduino_Uno.D9_PWM, MAX232.R2OUT
  N10: Arduino_Uno.D11_PWM/MOSI, R5_1.Pin_0
  N11: Arduino_Uno.D2, R7.Pin_0
  N12: Arduino_Uno.D5_PWM, R4.Pin_0
  5V: Arduino_Uno.5V, MAX232.VCC, C232_2.-
  N13: R2_1.Pin_0, R2_3.Pin_0
  N14: R3_1.Pin_0, R3_3.Pin_0
  N15: R4.Pin_1, C4.-
  N16: R5_1.Pin_1, R5_2.Pin_0, R6.Pin_0
  N17: C6.-, R6.Pin_1
  N18: MAX232.C1+, C232_1.-
  N19: MAX232.V+, C232_2.+
  N20: MAX232.C1-, C232_1.+
  N21: MAX232.C2+, C232_3.-
  N22: MAX232.C2-, C232_3.+
  N23: MAX232.V-, C232_4.-
  N24: MAX232.T2OUT, D-SUB.3
  N25: MAX232.R2IN, D-SUB.2
  N26: Q1.B, R7.Pin_1
  N27: Q1.C, R8.Pin_1
  N28: R8.Pin_0, V1.V+

notes:
  flow setpoint
  Ar + EtOH
  pressure, flowmeter
  (read)
  oven rs232
